// Logisim project main.circ as structural Verilog: 1 circuit, main circuit main
module main (
);

  wire and_1_out, cdm_16_1_p1, cdm_16_1_p2, cdm_16_1_p4, cdm_16_1_p5, cdm_16_1_p6, cdm_16_1_p7, clock, HS,
       I_Osel, in_out_prime, main_1_i_osel_2, main_1_in_out_prime_2, mem, not_1_out, RAM, word;
  wire [7:0] main_1_i_oaddr_2;
  wire [15:0] adr, cdm_16_1_p12, cdm_16_1_p13, data, main_1_i_odat_2;
  wire [31:0] main_1_out_10, main_1_out_11, main_1_out_12, main_1_out_13, main_1_out_14, main_1_out_15,
       main_1_out_16, main_1_out_17, main_1_out_18, main_1_out_19, main_1_out_20, main_1_out_21,
       main_1_out_22, main_1_out_23, main_1_out_24, main_1_out_25, main_1_out_26, main_1_out_27,
       main_1_out_28, main_1_out_29, main_1_out_30, main_1_out_31, main_1_out_32, main_1_out_33,
       main_1_out_34, main_1_out_35, main_1_out_36, main_1_out_37, main_1_out_38, main_1_out_39,
       main_1_out_40, main_1_out_41;

  // Probe on cdm_16_1_p1
  // Probe on cdm_16_1_p2
  // CdM_16 cdm_16_1: pin names not known; wires that end beside it: cdm_16_1_p1, cdm_16_1_p2, clock, cdm_16_1_p4, cdm_16_1_p5, cdm_16_1_p6, cdm_16_1_p7, mem, in_out_prime, word, adr, cdm_16_1_p12, cdm_16_1_p13
  Clock clock_1 (.out(clock));
  Button Hard_reset (.out(HS));
  // Probe on cdm_16_1_p4
  // Probe on cdm_16_1_p5
  DotMatrix #(.inputtype("row"), .matrixcols(32), .matrixrows(32)) dotmatrix_1 (
    .row0(main_1_out_10), .row1(main_1_out_11), .row2(main_1_out_12), .row3(main_1_out_13),
    .row4(main_1_out_14), .row5(main_1_out_15), .row6(main_1_out_16), .row7(main_1_out_17),
    .row8(main_1_out_18), .row9(main_1_out_19), .row10(main_1_out_20), .row11(main_1_out_21),
    .row12(main_1_out_22), .row13(main_1_out_23), .row14(main_1_out_24), .row15(main_1_out_25),
    .row16(main_1_out_26), .row17(main_1_out_27), .row18(main_1_out_28), .row19(main_1_out_29),
    .row20(main_1_out_30), .row21(main_1_out_31), .row22(main_1_out_32), .row23(main_1_out_33),
    .row24(main_1_out_34), .row25(main_1_out_35), .row26(main_1_out_36), .row27(main_1_out_37),
    .row28(main_1_out_38), .row29(main_1_out_39), .row30(main_1_out_40), .row31(main_1_out_41));
  matrixIO_main main_1 (
    .in_out_prime(in_out_prime), .I_Oaddr(adr[7:0]), .I_Osel(I_Osel), .I_Odat(data), .clock(clock),
    .in_out_prime_2(main_1_in_out_prime_2), .I_Oaddr_2(main_1_i_oaddr_2), .I_Osel_2(main_1_i_osel_2),
    .I_Odat_2(main_1_i_odat_2), .out_10(main_1_out_10), .out_11(main_1_out_11), .out_12(main_1_out_12),
    .out_13(main_1_out_13), .out_14(main_1_out_14), .out_15(main_1_out_15), .out_16(main_1_out_16),
    .out_17(main_1_out_17), .out_18(main_1_out_18), .out_19(main_1_out_19), .out_20(main_1_out_20),
    .out_21(main_1_out_21), .out_22(main_1_out_22), .out_23(main_1_out_23), .out_24(main_1_out_24),
    .out_25(main_1_out_25), .out_26(main_1_out_26), .out_27(main_1_out_27), .out_28(main_1_out_28),
    .out_29(main_1_out_29), .out_30(main_1_out_30), .out_31(main_1_out_31), .out_32(main_1_out_32),
    .out_33(main_1_out_33), .out_34(main_1_out_34), .out_35(main_1_out_35), .out_36(main_1_out_36),
    .out_37(main_1_out_37), .out_38(main_1_out_38), .out_39(main_1_out_39), .out_40(main_1_out_40),
    .out_41(main_1_out_41));
  // Probe on cdm_16_1_p6
  // Probe on cdm_16_1_p7
  // Probe on adr
  assign data = not_1_out ? cdm_16_1_p12 : 16'bz;  // Controlled_Buffer controlled_buffer_1
  not not_1 (not_1_out, in_out_prime);
  assign cdm_16_1_p13 = in_out_prime ? data : 16'bz;  // Controlled_Buffer controlled_buffer_2
  // RAM ram_1: pin names not known; wires that end beside it: adr, word, RAM, clock, in_out_prime, data
  // Probe on data
  and and_1 (and_1_out, adr[8], adr[9], adr[10], adr[11], adr[12], adr[13], adr[14], adr[15]);
  and and_2 (RAM, ~and_1_out, mem);  // AND_Gate
  and and_3 (I_Osel, mem, and_1_out);

  // Other names for the same wires on the sheet: I_Odat[15:0] = data; I_Oaddr[7:0] = adr[7:0];
  //   rd_wr_prime = in_out_prime
endmodule
